# Fritzing sketch nokia-lcd-5510 (saved by Fritzing 0.9.2b)
breadboards: 1

parts:
  Eleman1 = Arduino Pro Mini v13
  DHT1 = DHT11 Humitidy and Temperature Sensor

nets:
  N1: Eleman1.DTR, Eleman1.D0/TX
  GND: Eleman1.GND, DHT1.NULL, DHT1.GND

custom parts:
  DHT11 Humitidy and Temperature Sensor: DHT11 Humidity and Temperature Sensor
