# Fritzing sketch push-button (saved by Fritzing 0.9.2b)
breadboards: 1

parts:
  Part1 = Arduino Ethernet Shield (Rev3)
  LED1 = LED - 5mm [color="Red (633nm)" package="5 mm [THT]"]
  R1 = Resistor [tolerance=±5% resistance=100 package="2010 [SMD]"]
  S1 = Momentary Switch [package=ksa_sealed_tac_switch]
  R2 = Resistor [tolerance=±5% resistance=10k package=THT]

nets:
  N1: Part1.GND, LED1.cathode, R2.Pin_1
  N2: Part1.D8, S1.2, R2.Pin_0
  N3: Part1.SPI/D13, R1.Pin_1
  N4: Part1.5V, S1.4
  N5: LED1.anode, R1.Pin_0

// code stored in the sketch: Push Button.ino
const int LED_PIN = 13;
const int PUSH_BUTTON_PIN =8;

bool state = false;

void setup()
{
  pinMode(LED_PIN, OUTPUT);
  pinMode(PUSH_BUTTON_PIN, INPUT); 
  digitalWrite(LED_PIN, LOW);
  digitalWrite(PUSH_BUTTON_PIN, LOW);
}

void loop()
{
  if(digitalRead(PUSH_BUTTON_PIN) == HIGH){
   state = !state; 
    delay(300); 

  }
  
  if(state){
  	digitalWrite(LED_PIN, HIGH);
  }else{
    digitalWrite(LED_PIN, LOW);
  }
  
}

// code stored in the sketch: push-button.ino
const int LED_PIN = 13;
const int PUSH_BUTTON_PIN =8;

bool state = false;

void setup()
{
  pinMode(LED_PIN, OUTPUT);
  pinMode(PUSH_BUTTON_PIN, INPUT); 
  digitalWrite(LED_PIN, LOW);
  digitalWrite(PUSH_BUTTON_PIN, LOW);
}

void loop()
{
  if(digitalRead(PUSH_BUTTON_PIN) == HIGH){
   state = !state; 
    delay(300); 

  }
  
  if(state){
  	digitalWrite(LED_PIN, HIGH);
  }else{
    digitalWrite(LED_PIN, LOW);
  }
  
}
