# Fritzing sketch seven-segment (saved by Fritzing 0.9.2b)
breadboards: 1

parts:
  7_Segment1 = 7 Segment Display
  Eleman1 = Arduino Board Ethernet
  R1 = Resistor [tolerance=±5% resistance=220 package=THT]
  R2 = Resistor [tolerance=±5% resistance=220 package=THT]

nets:
  N1: 7_Segment1.Segment_D, Eleman1.D6_PWM, Eleman1.D7
  N2: 7_Segment1.common_cathode, R1.Pin_1, R2.Pin_1
  N3: 7_Segment1.Segment_C, Eleman1.D5_PWM
  N4: 7_Segment1.Segment_DP, Eleman1.D4
  N5: 7_Segment1.Segment_B, Eleman1.D8
  N6: 7_Segment1.Segment_A, Eleman1.D9_PWM
  N7: 7_Segment1.Segment_F, Eleman1.D10_PWM/SS
  N8: 7_Segment1.Segment_G, Eleman1.D11/MOSI
  N9: R1.Pin_0, R2.Pin_0

// code stored in the sketch: seven-segment.ino
const int ledPoint = 4;
const int led1 = 5;
const int led2 = 6;
const int led3 = 7;
const int led4 = 8;
const int led5 = 9;
const int led6 = 10;
const int led7 = 11;

void setup() {
  // put your setup code here, to run once:
  pinMode(ledPoint, OUTPUT);
  pinMode(led1, OUTPUT);
  pinMode(led2, OUTPUT);
  pinMode(led3, OUTPUT);
  pinMode(led4, OUTPUT);
  pinMode(led5, OUTPUT);
  pinMode(led6, OUTPUT);
  pinMode(led7, OUTPUT);

  clearDisplay();
}

void loop() { 
  for(int i = 9; i >= 0; i--)
  {
    displayNumber(i);
    delay(1000);  
  }
}

void clearDisplay(){
  digitalWrite(ledPoint, LOW);
  digitalWrite(led1, LOW);
  digitalWrite(led2, LOW);
  digitalWrite(led3, LOW);
  digitalWrite(led4, LOW);
  digitalWrite(led5, LOW);
  digitalWrite(led6, LOW);
  digitalWrite(led7, LOW);  
}

void displayNumber(int number){
  switch(number)
  {
    case 0:
      digitalWrite(led1, HIGH);
      digitalWrite(led2, HIGH);
      digitalWrite(led3, HIGH);
      digitalWrite(led4, HIGH);
      digitalWrite(led5, HIGH);
      digitalWrite(led6, HIGH);
      digitalWrite(led7, LOW);
      break;
    case 1:
      digitalWrite(led1, HIGH);
      digitalWrite(led2, LOW);
      digitalWrite(led3, LOW);
      digitalWrite(led4, HIGH);
      digitalWrite(led5, LOW);
      digitalWrite(led6, LOW);
      digitalWrite(led7, LOW);
      break;
    case 2:
      digitalWrite(led1, LOW);
      digitalWrite(led2, HIGH);
      digitalWrite(led3, HIGH);
      digitalWrite(led4, HIGH);
      digitalWrite(led5, HIGH);
      digitalWrite(led6, LOW);
      digitalWrite(led7, HIGH);
      break;
    case 3:
      digitalWrite(led1, HIGH);
      digitalWrite(led2, HIGH);
      digitalWrite(led3, LOW);
      digitalWrite(led4, HIGH);
      digitalWrite(led5, HIGH);
      digitalWrite(led6, LOW);
      digitalWrite(led7, HIGH);
      break;
    case 4:
      digitalWrite(led1, HIGH);
      digitalWrite(led2, LOW);
      digitalWrite(led3, LOW);
      digitalWrite(led4, HIGH);
      digitalWrite(led5, LOW);
      digitalWrite(led6, HIGH);
      digitalWrite(led7, HIGH);
      break;
    case 5:
      digitalWrite(led1, HIGH);
      digitalWrite(led2, HIGH);
      digitalWrite(led3, LOW);
      digitalWrite(led4, LOW);
      digitalWrite(led5, HIGH);
      digitalWrite(led6, HIGH);
      digitalWrite(led7, HIGH);
      break;
    case 6:
      digitalWrite(led1, HIGH);
      digitalWrite(led2, HIGH);
      digitalWrite(led3, HIGH);
      digitalWrite(led4, LOW);
      digitalWrite(led5, HIGH);
      digitalWrite(led6, HIGH);
      digitalWrite(led7, HIGH);
      break; 
    case 7:
      digitalWrite(led1, HIGH);
      digitalWrite(led2, LOW);
      digitalWrite(led3, LOW);
      digitalWrite(led4, HIGH);
      digitalWrite(led5, HIGH);
      digitalWrite(led6, LOW);
      digitalWrite(led7, LOW);
      break;    
    case 8:
      digitalWrite(led1, HIGH);
      digitalWrite(led2, HIGH);
      digitalWrite(led3, HIGH);
      digitalWrite(led4, HIGH);
      digitalWrite(led5, HIGH);
      digitalWrite(led6, HIGH);
      digitalWrite(led7, HIGH);
      break;
    case 9:
      digitalWrite(led1, HIGH);
      digitalWrite(led2, HIGH);
      digitalWrite(led3, LOW);
      digitalWrite(led4, HIGH);
      digitalWrite(led5, HIGH);
      digitalWrite(led6, HIGH);
      digitalWrite(led7, HIGH);
      break;              
  }
}
